// Logisim project COMPUTER.circ as structural Verilog: 30 circuits, main circuit main
module main (
  output [7:0] BUS_DATA_INT,
  output [7:0] BUS_DATA_UINT
);

  wire AI, AO, BI, BO, CE, CF, CLK, CO, EO, FI, HLT, II, IO, IR4, IR5, IR6, IR7, JUMP, MI, OI, RI, RO, SU, ZF;
  wire [3:0] controlled_buffer_1_out_2, register_1_q;
  wire [7:0] MAR_q, RAM16Byte_dout, Register_A_q, Register_B_q;
  wire [7:4] controlled_buffer_1_out;

  Register Register_A (
    .D({controlled_buffer_1_out, controlled_buffer_1_out_2}), .en(AI), .clk(CLK), .Q(Register_A_q));  // open: clr
  Register register_1 (
    .D({controlled_buffer_1_out, controlled_buffer_1_out_2}), .en(II), .clk(CLK),
    .Q({IR7, IR6, IR5, IR4, register_1_q}));  // open: clr
  assign {controlled_buffer_1_out, controlled_buffer_1_out_2} = AO ? Register_A_q : 8'bz;  // Controlled_Buffer controlled_buffer_1
  CLOCK0 clock0_1 (.HLT(HLT), .CLK_OUT(CLK));
  ALU alu_1 (
    .EO(EO), .IN_A(Register_A_q), .IN_B(Register_B_q), .CLK(CLK), .FI(FI), .SU(SU), .CF(CF), .ZF(ZF),
    .Sum({controlled_buffer_1_out, controlled_buffer_1_out_2}));
  assign {controlled_buffer_1_out, controlled_buffer_1_out_2} = IO ? {4'b0000, register_1_q} : 8'bz;  // Controlled_Buffer controlled_buffer_2
  PC pc_1 (
    .CO(CO), .CLK(CLK), .Jump(JUMP), .CE(CE),
    .Jump_Address({controlled_buffer_1_out, controlled_buffer_1_out_2}),
    .Data_Out({controlled_buffer_1_out, controlled_buffer_1_out_2}));
  CU cu_1 (
    .Instruction({IR7, IR6, IR5, IR4, 2'b00, CF, ZF}), .CLK(CLK), .AI(AI), .AO(AO), .BI(BI), .BO(BO),
    .EO(EO), .SUB(SU), .CE(CE), .CO(CO), .Jump(JUMP), .OI(OI), .HLT(HLT), .FI(FI), .MI(MI), .RI(RI), .RO(RO),
    .II(II), .IO(IO));
  Register #(.trigger("high")) MAR (
    .D({4'b0000, controlled_buffer_1_out_2}), .en(MI), .clk(CLK), .Q(MAR_q));  // open: clr
  Register Register_B (
    .D({controlled_buffer_1_out, controlled_buffer_1_out_2}), .en(BI), .clk(CLK), .Q(Register_B_q));  // open: clr
  assign {controlled_buffer_1_out, controlled_buffer_1_out_2} = BO ? Register_B_q : 8'bz;  // Controlled_Buffer controlled_buffer_3
  Register Register_Out (
    .D({controlled_buffer_1_out, controlled_buffer_1_out_2}), .en(OI), .clk(CLK), .Q(BUS_DATA_INT));  // open: clr
  RAM #(.addrWidth(4), .trigger("high")) RAM16Byte (
    .addr(MAR_q[3:0]), .we(RI), .oe(RO), .din({controlled_buffer_1_out, controlled_buffer_1_out_2}),
    .dout(RAM16Byte_dout));
  assign {controlled_buffer_1_out, controlled_buffer_1_out_2} = RO ? RAM16Byte_dout : 8'bz;  // Controlled_Buffer controlled_buffer_4

  assign BUS_DATA_UINT = BUS_DATA_INT;
endmodule

module NAND_Gate (
  input  A,
  input  B
);

  wire transistor_1_out;

  Transistor transistor_1 (.in(1'b1), .out(transistor_1_out), .gate(A));
  LED led_1 (.in(transistor_1_out));
  Transistor transistor_2 (.in(1'b1), .out(transistor_1_out), .gate(B));
endmodule

module NOT_Gate (
  input  A,
  output Q
);

  nand nand_1 (Q, A, A);
endmodule

module AND_Gate (
  input  A,
  input  B,
  output Q
);

  wire nand_1_out;

  nand nand_1 (nand_1_out, A, B);
  not not_1 (Q, nand_1_out);
endmodule

module OR_Gate (
  input  A,
  input  B,
  output Q
);

  wire not_1_out, not_2_out;

  not not_1 (not_1_out, A);
  not not_2 (not_2_out, B);
  nand nand_1 (Q, not_1_out, not_2_out);
endmodule

module XOR_Gate (
  input  A,
  input  B,
  output Q
);

  wire n1_out, n2_out, n3_out;

  nand n1 (n1_out, A, B);
  nand n2 (n2_out, A, n1_out);
  nand n3 (n3_out, n1_out, B);
  nand n4 (Q, n2_out, n3_out);
endmodule

module MUX (
  input  A,
  input  Selection,
  input  B,
  output Q
);

  wire n1_out, n2_out, not_1_out;

  not not_1 (not_1_out, Selection);
  nand n1 (n1_out, A, not_1_out);
  nand n2 (n2_out, Selection, B);
  nand n3 (Q, n1_out, n2_out);
endmodule

module MUX8 (
  input  Selection,
  input  [7:0] IN_A,
  input  [7:0] IN_B,
  output [7:0] out_4
);

  Multiplexer multiplexer_1 (.in0(IN_A[0]), .in1(IN_B[0]), .out(out_4[0]), .sel(Selection));
  Multiplexer multiplexer_2 (.in0(IN_A[1]), .in1(IN_B[1]), .out(out_4[1]), .sel(Selection));
  Multiplexer multiplexer_3 (.in0(IN_A[2]), .in1(IN_B[2]), .out(out_4[2]), .sel(Selection));
  Multiplexer multiplexer_4 (.in0(IN_A[3]), .in1(IN_B[3]), .out(out_4[3]), .sel(Selection));
  Multiplexer multiplexer_5 (.in0(IN_A[4]), .in1(IN_B[4]), .out(out_4[4]), .sel(Selection));
  Multiplexer multiplexer_6 (.in0(IN_A[5]), .in1(IN_B[5]), .out(out_4[5]), .sel(Selection));
  Multiplexer multiplexer_7 (.in0(IN_A[6]), .in1(IN_B[6]), .out(out_4[6]), .sel(Selection));
  Multiplexer multiplexer_8 (.in0(IN_A[7]), .in1(IN_B[7]), .out(out_4[7]), .sel(Selection));

  // Other names for the same wires on the sheet: A0 = IN_A[0]; A1 = IN_A[1]; A2 = IN_A[2]; A3 = IN_A[3]; A4 = IN_A[4];
  //   A5 = IN_A[5]; A6 = IN_A[6]; A7 = IN_A[7]; B0 = IN_B[0]; B1 = IN_B[1]; B2 = IN_B[2]; B3 = IN_B[3]; B4 = IN_B[4];
  //   B5 = IN_B[5]; B6 = IN_B[6]; B7 = IN_B[7]; OUT0 = out_4[0]; OUT1 = out_4[1]; OUT2 = out_4[2]; OUT3 = out_4[3];
  //   OUT4 = out_4[4]; OUT5 = out_4[5]; OUT6 = out_4[6]; OUT7 = out_4[7]
endmodule

module MUX8x4 (
  input  [7:0] IN_0,
  input  [7:0] IN_1,
  input  [7:0] IN_2,
  input  [7:0] IN_3,
  input  [1:0] SELECTION,
  output [7:0] Q
);

  wire [7:0] multiplexer_1_out, multiplexer_2_out;

  Multiplexer #(.width(8)) multiplexer_1 (.in0(IN_0), .in1(IN_1), .out(multiplexer_1_out), .sel(SELECTION[0]));
  Multiplexer #(.width(8)) multiplexer_2 (.in0(IN_2), .in1(IN_3), .out(multiplexer_2_out), .sel(SELECTION[0]));
  Multiplexer #(.width(8)) multiplexer_3 (
    .in0(multiplexer_1_out), .in1(multiplexer_2_out), .out(Q), .sel(SELECTION[1]));
endmodule

module MUX8x8 (
  input  [7:0] IN_0,
  input  [7:0] IN_1,
  input  [7:0] IN_2,
  input  [7:0] IN_3,
  input  [2:0] SELECTION,
  input  [7:0] IN_4,
  input  [7:0] IN_5,
  input  [7:0] IN_6,
  input  [7:0] IN_7,
  output [7:0] Q
);

  wire [7:0] multiplexer_1_out, multiplexer_2_out;

  Multiplexer #(.select(2), .width(8)) multiplexer_1 (
    .in0(IN_0), .in1(IN_1), .in2(IN_2), .in3(IN_3), .out(multiplexer_1_out), .sel(SELECTION[1:0]));
  Multiplexer #(.select(2), .width(8)) multiplexer_2 (
    .in0(IN_4), .in1(IN_5), .in2(IN_6), .in3(IN_7), .out(multiplexer_2_out), .sel(SELECTION[1:0]));
  Multiplexer #(.width(8)) multiplexer_3 (
    .in0(multiplexer_1_out), .in1(multiplexer_2_out), .out(Q), .sel(SELECTION[2]));
endmodule

module MUX8x16 (
  input  [7:0] IN_0,
  input  [7:0] IN_1,
  input  [7:0] IN_2,
  input  [7:0] IN_3,
  input  [7:0] IN_4,
  input  [7:0] IN_5,
  input  [7:0] IN_6,
  input  [7:0] IN_7,
  input  [3:0] SELECTION,
  input  [7:0] IN_8,
  input  [7:0] IN_9,
  input  [7:0] IN_10,
  input  [7:0] IN_11,
  input  [7:0] IN_12,
  input  [7:0] IN_13,
  input  [7:0] IN_14,
  input  [7:0] IN_15,
  output [7:0] Q
);

  wire [7:0] multiplexer_1_out, multiplexer_2_out;

  Multiplexer #(.select(3), .width(8)) multiplexer_1 (
    .in0(IN_0), .in1(IN_1), .in2(IN_2), .in3(IN_3), .in4(IN_4), .in5(IN_5), .in6(IN_6), .in7(IN_7),
    .out(multiplexer_1_out), .sel(SELECTION[2:0]));
  Multiplexer #(.select(3), .width(8)) multiplexer_2 (
    .in0(IN_8), .in1(IN_9), .in2(IN_10), .in3(IN_11), .in4(IN_12), .in5(IN_13), .in6(IN_14), .in7(IN_15),
    .out(multiplexer_2_out), .sel(SELECTION[2:0]));
  Multiplexer #(.width(8)) multiplexer_3 (
    .in0(multiplexer_1_out), .in1(multiplexer_2_out), .out(Q), .sel(SELECTION[3]));
endmodule

module Decoder3In (
  input  [2:0] SELECTION,
  input  ENABLE,
  output OUT0,
  output OUT1,
  output OUT2,
  output OUT3,
  output OUT4,
  output OUT5,
  output OUT6,
  output OUT7
);

  wire not_1_out, not_2_out, not_3_out;

  not not_1 (not_1_out, SELECTION[0]);
  not not_2 (not_2_out, SELECTION[1]);
  not not_3 (not_3_out, SELECTION[2]);
  and and_1 (OUT0, not_1_out, not_2_out, not_3_out, ENABLE);
  and and_2 (OUT1, SELECTION[0], not_2_out, not_3_out, ENABLE);
  and and_3 (OUT2, not_1_out, SELECTION[1], not_3_out, ENABLE);
  and and_4 (OUT3, SELECTION[0], SELECTION[1], not_3_out, ENABLE);
  and and_5 (OUT4, not_1_out, not_2_out, SELECTION[2], ENABLE);
  and and_6 (OUT5, SELECTION[0], not_2_out, SELECTION[2], ENABLE);
  and and_7 (OUT6, not_1_out, SELECTION[1], SELECTION[2], ENABLE);
  and and_8 (OUT7, SELECTION[0], SELECTION[1], SELECTION[2], ENABLE);
endmodule

module Decoder4In (
  input  [3:0] SELECTION,
  input  ENABLE,
  output OUT0,
  output OUT1,
  output OUT2,
  output OUT3,
  output OUT4,
  output OUT5,
  output OUT6,
  output OUT7,
  output OUT8,
  output OUT9,
  output OUT10,
  output OUT11,
  output OUT12,
  output OUT13,
  output OUT14,
  output OUT15
);

  wire NOT_IN0, NOT_IN1, NOT_IN2, NOT_IN3;

  not not_1 (NOT_IN0, SELECTION[0]);
  not not_2 (NOT_IN1, SELECTION[1]);
  not not_3 (NOT_IN2, SELECTION[2]);
  not not_4 (NOT_IN3, SELECTION[3]);
  and and_1 (OUT0, NOT_IN0, NOT_IN1, NOT_IN2, NOT_IN3, ENABLE);
  and and_2 (OUT1, SELECTION[0], NOT_IN1, NOT_IN2, NOT_IN3, ENABLE);
  and and_3 (OUT2, NOT_IN0, SELECTION[1], NOT_IN2, NOT_IN3, ENABLE);
  and and_4 (OUT3, SELECTION[0], SELECTION[1], NOT_IN2, NOT_IN3, ENABLE);
  and and_5 (OUT4, NOT_IN0, NOT_IN1, SELECTION[2], NOT_IN3, ENABLE);
  and and_6 (OUT5, SELECTION[0], NOT_IN1, SELECTION[2], NOT_IN3, ENABLE);
  and and_7 (OUT6, NOT_IN0, SELECTION[1], SELECTION[2], NOT_IN3, ENABLE);
  and and_8 (OUT7, SELECTION[0], SELECTION[1], SELECTION[2], NOT_IN3, ENABLE);
  and and_9 (OUT8, NOT_IN0, NOT_IN1, NOT_IN2, SELECTION[3], ENABLE);
  and and_10 (OUT9, SELECTION[0], NOT_IN1, NOT_IN2, SELECTION[3], ENABLE);
  and and_11 (OUT10, NOT_IN0, SELECTION[1], NOT_IN2, SELECTION[3], ENABLE);
  and and_12 (OUT11, SELECTION[0], SELECTION[1], NOT_IN2, SELECTION[3], ENABLE);
  and and_13 (OUT12, NOT_IN0, NOT_IN1, SELECTION[2], SELECTION[3], ENABLE);
  and and_14 (OUT13, SELECTION[0], NOT_IN1, SELECTION[2], SELECTION[3], ENABLE);
  and and_15 (OUT14, NOT_IN0, SELECTION[1], SELECTION[2], SELECTION[3], ENABLE);
  and and_16 (OUT15, SELECTION[0], SELECTION[1], SELECTION[2], SELECTION[3], ENABLE);

  // Other names for the same wires on the sheet: IN0 = SELECTION[0]; IN1 = SELECTION[1]; IN2 = SELECTION[2];
  //   IN3 = SELECTION[3]
endmodule

module ControlledBuffer1 (
  input  Data_In,
  input  Enable,
  output Data_Out
);

  wire and_1_out, nand_1_out, not_1_out;

  not not_1 (not_1_out, Data_In);
  nand nand_1 (nand_1_out, Data_In, Enable);
  and and_1 (and_1_out, not_1_out, Enable);
  Transistor transistor_1 (.in(1'b1), .out(Data_Out), .gate(nand_1_out));
  Transistor #(.\type ("n")) transistor_2 (.in(1'b0), .out(Data_Out), .gate(and_1_out));
endmodule

module ControlledBuffer8 (
  input  Enable,
  input  [7:0] Data_In,
  output [7:0] Data_Out
);

  assign Data_Out[0] = Enable ? Data_In[0] : 1'bz;  // Controlled_Buffer controlled_buffer_1
  assign Data_Out[1] = Enable ? Data_In[1] : 1'bz;  // Controlled_Buffer controlled_buffer_2
  assign Data_Out[2] = Enable ? Data_In[2] : 1'bz;  // Controlled_Buffer controlled_buffer_3
  assign Data_Out[3] = Enable ? Data_In[3] : 1'bz;  // Controlled_Buffer controlled_buffer_4
  assign Data_Out[4] = Enable ? Data_In[4] : 1'bz;  // Controlled_Buffer controlled_buffer_5
  assign Data_Out[5] = Enable ? Data_In[5] : 1'bz;  // Controlled_Buffer controlled_buffer_6
  assign Data_Out[6] = Enable ? Data_In[6] : 1'bz;  // Controlled_Buffer controlled_buffer_7
  assign Data_Out[7] = Enable ? Data_In[7] : 1'bz;  // Controlled_Buffer controlled_buffer_8
endmodule

module Half_Adder (
  input  IN_A,
  input  IN_B,
  output Carry,
  output Sum
);

  and and_1 (Carry, IN_A, IN_B);
  xor xor_1 (Sum, IN_A, IN_B);
endmodule

module Full_Adder (
  input  IN_A,
  input  IN_B,
  input  IN_C,
  output Carry,
  output Sum
);

  wire half_adder_1_carry, half_adder_1_sum, half_adder_2_carry;

  Half_Adder half_adder_1 (.IN_A(IN_A), .IN_B(IN_B), .Carry(half_adder_1_carry), .Sum(half_adder_1_sum));
  or or_1 (Carry, half_adder_1_carry, half_adder_2_carry);
  Half_Adder half_adder_2 (.IN_A(half_adder_1_sum), .IN_B(IN_C), .Carry(half_adder_2_carry), .Sum(Sum));
endmodule

module ALU (
  input  [7:0] IN_A,
  input  CLK,
  input  FI,
  input  [7:0] IN_B,
  input  SU,
  input  EO,
  output [7:0] Sum,
  output CF,
  output ZF
);

  wire and_1_out, and_2_out, full_adder_1_carry, full_adder_2_carry, full_adder_3_carry, full_adder_4_carry,
       full_adder_5_carry, full_adder_6_carry, full_adder_7_carry, IN_B0, IN_B1, IN_B2, IN_B3, IN_B4, IN_B5,
       IN_B6, IN_B7, nor_1_out, nor_2_out, nor_3_out, nor_4_out, OUT_0, OUT_1, OUT_2, OUT_3, OUT_4, OUT_5,
       OUT_6, OUT_7;
  wire [7:0] full_adder_8_carry;
  wire [7:2] register_1_q;

  xor xor_1 (IN_B7, SU, IN_B[7]);
  xor xor_2 (IN_B6, SU, IN_B[6]);
  xor xor_3 (IN_B5, SU, IN_B[5]);
  Full_Adder full_adder_1 (.IN_A(IN_A[0]), .IN_B(SU), .IN_C(IN_B0), .Carry(full_adder_1_carry), .Sum(OUT_0));
  xor xor_4 (IN_B4, SU, IN_B[4]);
  xor xor_5 (IN_B3, SU, IN_B[3]);
  xor xor_6 (IN_B2, SU, IN_B[2]);
  Full_Adder full_adder_2 (
    .IN_A(IN_A[1]), .IN_B(full_adder_1_carry), .IN_C(IN_B1), .Carry(full_adder_2_carry), .Sum(OUT_1));
  assign Sum = EO ? {OUT_7, OUT_6, OUT_5, OUT_4, OUT_3, OUT_2, OUT_1, OUT_0} : 8'bz;  // Controlled_Buffer controlled_buffer_1
  xor xor_7 (IN_B1, SU, IN_B[1]);
  xor xor_8 (IN_B0, SU, IN_B[0]);
  Full_Adder full_adder_3 (
    .IN_A(IN_A[2]), .IN_B(full_adder_2_carry), .IN_C(IN_B2), .Carry(full_adder_3_carry), .Sum(OUT_2));
  Full_Adder full_adder_4 (
    .IN_A(IN_A[3]), .IN_B(full_adder_3_carry), .IN_C(IN_B3), .Carry(full_adder_4_carry), .Sum(OUT_3));
  Full_Adder full_adder_5 (
    .IN_A(IN_A[4]), .IN_B(full_adder_4_carry), .IN_C(IN_B4), .Carry(full_adder_5_carry), .Sum(OUT_4));
  nor nor_1 (nor_1_out, OUT_0, OUT_1);
  nor nor_2 (nor_2_out, OUT_2, OUT_3);
  nor nor_3 (nor_3_out, OUT_4, OUT_5);
  nor nor_4 (nor_4_out, OUT_6, OUT_7);
  Full_Adder full_adder_6 (
    .IN_A(IN_A[5]), .IN_B(full_adder_5_carry), .IN_C(IN_B5), .Carry(full_adder_6_carry), .Sum(OUT_5));
  and and_1 (and_1_out, nor_1_out, nor_2_out);
  and and_2 (and_2_out, nor_3_out, nor_4_out);
  and and_3 (full_adder_8_carry[1], and_1_out, and_2_out);
  Full_Adder full_adder_7 (
    .IN_A(IN_A[6]), .IN_B(full_adder_6_carry), .IN_C(IN_B6), .Carry(full_adder_7_carry), .Sum(OUT_6));
  Full_Adder full_adder_8 (
    .IN_A(IN_A[7]), .IN_B(full_adder_7_carry), .IN_C(IN_B7), .Carry(full_adder_8_carry[0]), .Sum(OUT_7));
  Register register_1 (.D(full_adder_8_carry), .en(FI), .clk(CLK), .Q({register_1_q, ZF, CF}));  // open: clr

  // Notes on the sheet:
  //   Zero Checker
endmodule

module SRLatch (
  input  S,
  input  R,
  output Q
);

  wire nor_1_out;

  nor nor_1 (nor_1_out, S, Q);
  nor nor_2 (Q, nor_1_out, R);
endmodule

module GatedSRLatch (
  input  S,
  input  E,
  input  R,
  output Q
);

  wire and_1_out, and_2_out, nor_1_out;

  and and_1 (and_1_out, S, E);
  and and_2 (and_2_out, E, R);
  nor nor_1 (nor_1_out, and_1_out, Q);
  nor nor_2 (Q, nor_1_out, and_2_out);
endmodule

module DLatch (
  input  D,
  input  E,
  output Q
);

  wire and_1_out, and_2_out, nor_1_out, not_1_out, or_1_out, por_1_out;

  POR #(.PorHighDuration(1)) por_1 (.out(por_1_out));
  or or_1 (or_1_out, E, por_1_out);
  not not_1 (not_1_out, D);
  and and_1 (and_1_out, D, or_1_out);
  and and_2 (and_2_out, or_1_out, not_1_out);
  nor nor_1 (nor_1_out, and_1_out, Q);
  nor nor_2 (Q, nor_1_out, and_2_out);
endmodule

module JKLatch (
  input  J,
  input  E,
  input  K,
  input  in_4,
  input  in_5,
  input  in_6,
  output Q,
  output out_8
);

  wire and_1_out, and_2_out, nor_1_out;

  J_K_Flip_Flop j_k_ff_1 (.J(in_4), .K(in_5), .clk(in_6), .Q(out_8));  // open: Qn, preset, reset
  and and_1 (and_1_out, nor_1_out, J, E);
  and and_2 (and_2_out, E, K, Q);
  nor nor_1 (nor_1_out, and_1_out, Q);
  nor nor_2 (Q, nor_1_out, and_2_out);
endmodule

module Example (
  input  [7:0] A,
  input  [7:0] B,
  input  [7:0] C,
  input  [7:0] D,
  output [7:0] out_5
);

  wire clock_1_out, clock_2_out;
  wire [7:0] adder_1_out, adder_2_out, adder_3_out;

  Adder adder_1 (.a(A), .b(B), .out(adder_1_out));  // open: cin, cout
  Adder adder_2 (.a(C), .b(D), .out(adder_2_out));  // open: cin, cout
  Clock clock_1 (.out(clock_1_out));
  D_Flip_Flop d_ff_1 (.clk(clock_1_out));  // open: D, Q, Qn, preset, reset
  Adder adder_3 (.a(adder_1_out), .b(adder_2_out), .out(adder_3_out));  // open: cin, cout
  Clock clock_2 (.out(clock_2_out));
  Register #(.trigger("high")) register_1 (.D(adder_3_out), .clk(clock_2_out), .Q(out_5));  // open: en, clr

  // Notes on the sheet:
  //   8Bit Adder
  //   8Bit Adder
  //   8Bit Adder
endmodule

module CLOCK0 (
  input  HLT,
  output CLK_OUT
);

  wire clock_1_out, not_1_out;

  Clock clock_1 (.out(clock_1_out));
  not not_1 (not_1_out, HLT);
  assign CLK_OUT = not_1_out ? clock_1_out : 1'bz;  // Controlled_Buffer controlled_buffer_1
endmodule

module Register8HighLevel (
  input  Enable,
  input  [7:0] Data,
  input  LOAD,
  output [7:0] out_4
);

  wire [3:0] d_ff_1_q, d_ff_5_q;

  D_Flip_Flop #(.trigger("high")) d_ff_1 (.D(Data[0]), .clk(LOAD), .Q(d_ff_1_q[0]));  // open: Qn, preset, reset
  D_Flip_Flop #(.trigger("high")) d_ff_2 (.D(Data[1]), .clk(LOAD), .Q(d_ff_1_q[1]));  // open: Qn, preset, reset
  D_Flip_Flop #(.trigger("high")) d_ff_3 (.D(Data[2]), .clk(LOAD), .Q(d_ff_1_q[2]));  // open: Qn, preset, reset
  D_Flip_Flop #(.trigger("high")) d_ff_4 (.D(Data[3]), .clk(LOAD), .Q(d_ff_1_q[3]));  // open: Qn, preset, reset
  D_Flip_Flop #(.trigger("high")) d_ff_5 (.D(Data[4]), .clk(LOAD), .Q(d_ff_5_q[0]));  // open: Qn, preset, reset
  D_Flip_Flop #(.trigger("high")) d_ff_6 (.D(Data[5]), .clk(LOAD), .Q(d_ff_5_q[1]));  // open: Qn, preset, reset
  D_Flip_Flop #(.trigger("high")) d_ff_7 (.D(Data[6]), .clk(LOAD), .Q(d_ff_5_q[2]));  // open: Qn, preset, reset
  D_Flip_Flop #(.trigger("high")) d_ff_8 (.D(Data[7]), .clk(LOAD), .Q(d_ff_5_q[3]));  // open: Qn, preset, reset
  Hex_Digit_Display hex_digit_display_1 (.value(d_ff_5_q));  // open: dp
  Hex_Digit_Display hex_digit_display_2 (.value(d_ff_1_q));  // open: dp
  assign out_4[0] = Enable ? d_ff_1_q[0] : 1'bz;  // Controlled_Buffer controlled_buffer_1
  assign out_4[1] = Enable ? d_ff_1_q[1] : 1'bz;  // Controlled_Buffer controlled_buffer_2
  assign out_4[2] = Enable ? d_ff_1_q[2] : 1'bz;  // Controlled_Buffer controlled_buffer_3
  assign out_4[3] = Enable ? d_ff_1_q[3] : 1'bz;  // Controlled_Buffer controlled_buffer_4
  assign out_4[4] = Enable ? d_ff_5_q[0] : 1'bz;  // Controlled_Buffer controlled_buffer_5
  assign out_4[5] = Enable ? d_ff_5_q[1] : 1'bz;  // Controlled_Buffer controlled_buffer_6
  assign out_4[6] = Enable ? d_ff_5_q[2] : 1'bz;  // Controlled_Buffer controlled_buffer_7
  assign out_4[7] = Enable ? d_ff_5_q[3] : 1'bz;  // Controlled_Buffer controlled_buffer_8
endmodule

module RAM8x16HighLevel (
  input  [3:0] ADDRESS,
  input  [7:0] DATA_IN,
  input  ENABLE_OUT,
  input  ENABLE_WRITE,
  output [7:0] out_5
);

  wire decoder4in_1_out0, decoder4in_1_out1, decoder4in_1_out2, decoder4in_1_out3, decoder4in_1_out4,
       decoder4in_1_out5, decoder4in_1_out6, decoder4in_1_out7, decoder4in_1_out8, decoder4in_1_out9,
       decoder4in_1_out10, decoder4in_1_out11, decoder4in_1_out12, decoder4in_1_out13, decoder4in_1_out14,
       decoder4in_1_out15;
  wire [7:0] register8highlevel_1_out_4, register8highlevel_2_out_4, register8highlevel_3_out_4,
       register8highlevel_4_out_4, register8highlevel_5_out_4, register8highlevel_6_out_4,
       register8highlevel_7_out_4, register8highlevel_8_out_4, register8highlevel_9_out_4,
       register8highlevel_10_out_4, register8highlevel_11_out_4, register8highlevel_12_out_4,
       register8highlevel_13_out_4, register8highlevel_14_out_4, register8highlevel_15_out_4,
       register8highlevel_16_out_4;

  Decoder4In decoder4in_1 (
    .SELECTION(ADDRESS), .ENABLE(ENABLE_WRITE), .OUT0(decoder4in_1_out0), .OUT1(decoder4in_1_out1),
    .OUT2(decoder4in_1_out2), .OUT3(decoder4in_1_out3), .OUT4(decoder4in_1_out4), .OUT5(decoder4in_1_out5),
    .OUT6(decoder4in_1_out6), .OUT7(decoder4in_1_out7), .OUT8(decoder4in_1_out8), .OUT9(decoder4in_1_out9),
    .OUT10(decoder4in_1_out10), .OUT11(decoder4in_1_out11), .OUT12(decoder4in_1_out12),
    .OUT13(decoder4in_1_out13), .OUT14(decoder4in_1_out14), .OUT15(decoder4in_1_out15));
  Register8HighLevel register8highlevel_1 (
    .Enable(ENABLE_OUT), .LOAD(decoder4in_1_out0), .Data(DATA_IN), .out_4(register8highlevel_1_out_4));
  Register8HighLevel register8highlevel_2 (
    .Enable(ENABLE_OUT), .LOAD(decoder4in_1_out1), .Data(DATA_IN), .out_4(register8highlevel_2_out_4));
  Register8HighLevel register8highlevel_3 (
    .Enable(ENABLE_OUT), .LOAD(decoder4in_1_out2), .Data(DATA_IN), .out_4(register8highlevel_3_out_4));
  Register8HighLevel register8highlevel_4 (
    .Enable(ENABLE_OUT), .LOAD(decoder4in_1_out3), .Data(DATA_IN), .out_4(register8highlevel_4_out_4));
  Register8HighLevel register8highlevel_5 (
    .Enable(ENABLE_OUT), .LOAD(decoder4in_1_out4), .Data(DATA_IN), .out_4(register8highlevel_5_out_4));
  Register8HighLevel register8highlevel_6 (
    .Enable(ENABLE_OUT), .LOAD(decoder4in_1_out5), .Data(DATA_IN), .out_4(register8highlevel_6_out_4));
  Register8HighLevel register8highlevel_7 (
    .Enable(ENABLE_OUT), .LOAD(decoder4in_1_out6), .Data(DATA_IN), .out_4(register8highlevel_7_out_4));
  Register8HighLevel register8highlevel_8 (
    .Enable(ENABLE_OUT), .LOAD(decoder4in_1_out7), .Data(DATA_IN), .out_4(register8highlevel_8_out_4));
  Register8HighLevel register8highlevel_9 (
    .Enable(ENABLE_OUT), .LOAD(decoder4in_1_out8), .Data(DATA_IN), .out_4(register8highlevel_9_out_4));
  Register8HighLevel register8highlevel_10 (
    .Enable(ENABLE_OUT), .LOAD(decoder4in_1_out9), .Data(DATA_IN), .out_4(register8highlevel_10_out_4));
  Register8HighLevel register8highlevel_11 (
    .Enable(ENABLE_OUT), .LOAD(decoder4in_1_out10), .Data(DATA_IN), .out_4(register8highlevel_11_out_4));
  Register8HighLevel register8highlevel_12 (
    .Enable(ENABLE_OUT), .LOAD(decoder4in_1_out11), .Data(DATA_IN), .out_4(register8highlevel_12_out_4));
  Register8HighLevel register8highlevel_13 (
    .Enable(ENABLE_OUT), .LOAD(decoder4in_1_out12), .Data(DATA_IN), .out_4(register8highlevel_13_out_4));
  Register8HighLevel register8highlevel_14 (
    .Enable(ENABLE_OUT), .LOAD(decoder4in_1_out13), .Data(DATA_IN), .out_4(register8highlevel_14_out_4));
  Register8HighLevel register8highlevel_15 (
    .Enable(ENABLE_OUT), .LOAD(decoder4in_1_out14), .Data(DATA_IN), .out_4(register8highlevel_15_out_4));
  Register8HighLevel register8highlevel_16 (
    .Enable(ENABLE_OUT), .LOAD(decoder4in_1_out15), .Data(DATA_IN), .out_4(register8highlevel_16_out_4));
  Multiplexer #(.select(4), .width(8)) multiplexer_1 (
    .in0(register8highlevel_1_out_4), .in1(register8highlevel_2_out_4), .in2(register8highlevel_3_out_4),
    .in3(register8highlevel_4_out_4), .in4(register8highlevel_5_out_4), .in5(register8highlevel_6_out_4),
    .in6(register8highlevel_7_out_4), .in7(register8highlevel_8_out_4), .in8(register8highlevel_9_out_4),
    .in9(register8highlevel_10_out_4), .in10(register8highlevel_11_out_4),
    .in11(register8highlevel_12_out_4), .in12(register8highlevel_13_out_4),
    .in13(register8highlevel_14_out_4), .in14(register8highlevel_15_out_4),
    .in15(register8highlevel_16_out_4), .out(out_5), .sel(ADDRESS));
endmodule

module ComputerWithoutCU (
  input  CO,
  input  Jump,
  input  CE,
  input  [7:0] in_4,
  input  BUS_IN,
  input  MI,
  input  RI,
  input  RO,
  input  II,
  input  IO,
  input  AI,
  input  AO,
  input  BI,
  input  BO,
  input  EO,
  input  SU,
  output [7:0] BUS_DATA_INT,
  output [7:0] BUS_DATA_UINT
);

  wire CF, CLK, FI, HLT, IR4, IR5, IR6, IR7, OI, ZF;
  wire [3:0] controlled_buffer_1_out, register_1_q;
  wire [7:0] MAR_q, RAM16Byte_dout, Register_A_q, Register_B_q;
  wire [7:4] controlled_buffer_1_out_2;

  Register Register_A (
    .D({controlled_buffer_1_out_2, controlled_buffer_1_out}), .en(AI), .clk(CLK), .Q(Register_A_q));  // open: clr
  assign {controlled_buffer_1_out_2, controlled_buffer_1_out} = AO ? Register_A_q : 8'bz;  // Controlled_Buffer controlled_buffer_1
  Register register_1 (
    .D({controlled_buffer_1_out_2, controlled_buffer_1_out}), .en(II), .clk(CLK),
    .Q({IR7, IR6, IR5, IR4, register_1_q}));  // open: clr
  ALU alu_1 (
    .EO(EO), .IN_A(Register_A_q), .IN_B(Register_B_q), .CLK(CLK), .FI(FI), .SU(SU), .CF(CF), .ZF(ZF),
    .Sum({controlled_buffer_1_out_2, controlled_buffer_1_out}));
  CLOCK0 clock0_1 (.HLT(HLT), .CLK_OUT(CLK));
  PC pc_1 (
    .CO(CO), .CLK(CLK), .Jump(Jump), .CE(CE),
    .Jump_Address({controlled_buffer_1_out_2, controlled_buffer_1_out}),
    .Data_Out({controlled_buffer_1_out_2, controlled_buffer_1_out}));
  assign {controlled_buffer_1_out_2, controlled_buffer_1_out} = IO ? {4'b0000, register_1_q} : 8'bz;  // Controlled_Buffer controlled_buffer_2
  Register #(.trigger("high")) MAR (
    .D({4'b0000, controlled_buffer_1_out}), .en(MI), .clk(CLK), .Q(MAR_q));  // open: clr
  assign {controlled_buffer_1_out_2, controlled_buffer_1_out} = BUS_IN ? in_4 : 8'bz;  // Controlled_Buffer controlled_buffer_3
  Register Register_B (
    .D({controlled_buffer_1_out_2, controlled_buffer_1_out}), .en(BI), .clk(CLK), .Q(Register_B_q));  // open: clr
  assign {controlled_buffer_1_out_2, controlled_buffer_1_out} = BO ? Register_B_q : 8'bz;  // Controlled_Buffer controlled_buffer_4
  RAM #(.addrWidth(4), .trigger("high")) RAM16Byte (
    .addr(MAR_q[3:0]), .we(RI), .oe(RO), .din({controlled_buffer_1_out_2, controlled_buffer_1_out}),
    .dout(RAM16Byte_dout));
  Register Register_Out (
    .D({controlled_buffer_1_out_2, controlled_buffer_1_out}), .en(OI), .clk(CLK), .Q(BUS_DATA_INT));  // open: clr
  assign {controlled_buffer_1_out_2, controlled_buffer_1_out} = RO ? RAM16Byte_dout : 8'bz;  // Controlled_Buffer controlled_buffer_5

  assign BUS_DATA_UINT = BUS_DATA_INT;
endmodule

module PC (
  input  CLK,
  input  Jump,
  input  [7:0] Jump_Address,
  input  CO,
  input  CE,
  output [7:0] Data_Out
);

  wire and_1_out, and_2_out, and_3_out, and_4_out, and_5_out, and_6_out, and_7_out, and_8_out, and_9_out,
       and_10_out, and_11_out, and_12_out, not_1_out, not_2_out, not_3_out, not_4_out, not_5_out, or_1_out,
       or_2_out, or_3_out, or_4_out, or_5_out, or_6_out, or_7_out, or_8_out, OUT_0, OUT_1, OUT_2, OUT_3;

  not not_1 (not_1_out, Jump);
  not not_2 (not_2_out, Jump_Address[0]);
  not not_3 (not_3_out, Jump_Address[1]);
  not not_4 (not_4_out, Jump_Address[2]);
  not not_5 (not_5_out, Jump_Address[3]);
  and and_1 (and_1_out, CE, not_1_out);
  and and_2 (and_2_out, Jump_Address[0], Jump);
  and and_3 (and_3_out, not_2_out, Jump);
  and and_4 (and_4_out, Jump_Address[1], Jump);
  and and_5 (and_5_out, not_3_out, Jump);
  and and_6 (and_6_out, Jump_Address[2], Jump);
  and and_7 (and_7_out, not_4_out, Jump);
  and and_8 (and_8_out, Jump_Address[3], Jump);
  and and_9 (and_9_out, not_5_out, Jump);
  or or_1 (or_1_out, and_2_out, and_1_out);
  or or_2 (or_2_out, and_3_out, and_1_out);
  and and_10 (and_10_out, and_1_out, OUT_0);
  or or_3 (or_3_out, and_4_out, and_10_out);
  or or_4 (or_4_out, and_5_out, and_10_out);
  and and_11 (and_11_out, and_10_out, OUT_1);
  or or_5 (or_5_out, and_6_out, and_11_out);
  or or_6 (or_6_out, and_7_out, and_11_out);
  and and_12 (and_12_out, and_11_out, OUT_2);
  or or_7 (or_7_out, and_8_out, and_12_out);
  or or_8 (or_8_out, and_9_out, and_12_out);
  J_K_Flip_Flop j_k_ff_1 (.J(or_1_out), .K(or_2_out), .clk(CLK), .Q(OUT_0));  // open: Qn, preset, reset
  J_K_Flip_Flop j_k_ff_2 (.J(or_3_out), .K(or_4_out), .clk(CLK), .Q(OUT_1));  // open: Qn, preset, reset
  J_K_Flip_Flop j_k_ff_3 (.J(or_5_out), .K(or_6_out), .clk(CLK), .Q(OUT_2));  // open: Qn, preset, reset
  J_K_Flip_Flop j_k_ff_4 (.J(or_7_out), .K(or_8_out), .clk(CLK), .Q(OUT_3));  // open: Qn, preset, reset
  assign Data_Out = CO ? {4'b0000, OUT_3, OUT_2, OUT_1, OUT_0} : 8'bz;  // Controlled_Buffer controlled_buffer_1

  // Other names for the same wires on the sheet: IN_0 = Jump_Address[0]; IN_1 = Jump_Address[1];
  //   IN_2 = Jump_Address[2]; IN_3 = Jump_Address[3]
endmodule

module SC (
  input  CLK,
  input  Reset,
  input  CE,
  output [7:0] Data_Out
);

  wire and_1_out, and_2_out, and_3_out;

  and and_1 (and_1_out, CE, Data_Out[0]);
  and and_2 (and_2_out, and_1_out, Data_Out[1]);
  and and_3 (and_3_out, and_2_out, Data_Out[2]);
  J_K_Flip_Flop j_k_ff_1 (.J(CE), .K(CE), .clk(CLK), .Q(Data_Out[0]), .reset(Reset));  // open: Qn, preset
  J_K_Flip_Flop j_k_ff_2 (.J(and_1_out), .K(and_1_out), .clk(CLK), .Q(Data_Out[1]), .reset(Reset));  // open: Qn, preset
  J_K_Flip_Flop j_k_ff_3 (.J(and_2_out), .K(and_2_out), .clk(CLK), .Q(Data_Out[2]), .reset(Reset));  // open: Qn, preset
  J_K_Flip_Flop j_k_ff_4 (.J(and_3_out), .K(and_3_out), .clk(CLK), .Q(Data_Out[3]), .reset(Reset));  // open: Qn, preset
  LED led_1 (.in(Data_Out[0]));
  LED led_2 (.in(Data_Out[1]));
  LED led_3 (.in(Data_Out[2]));

  assign Data_Out[7:4] = 4'b0000;

  // Other names for the same wires on the sheet: OUT_0 = Data_Out[0]; OUT_1 = Data_Out[1]; OUT_2 = Data_Out[2];
  //   OUT_3 = Data_Out[3]
endmodule

module CU (
  input  [7:0] Instruction,
  input  CLK,
  output MI,
  output RI,
  output RO,
  output II,
  output IO,
  output AI,
  output AO,
  output BI,
  output BO,
  output EO,
  output SUB,
  output CE,
  output CO,
  output Jump,
  output OI,
  output HLT,
  output FI
);

  wire ADD0, ADD1, ADD2, and_1_out, and_2_out, and_3_out, and_4_out, and_5_out, and_6_out, and_7_out,
       and_8_out, and_9_out, and_10_out, JMP0, JMPC0, JMPZ0, LOADA0, LOADA1, LOADI0, not_1_out, not_2_out,
       not_3_out, not_4_out, not_5_out, not_6_out, not_7_out, not_8_out, not_9_out, not_10_out, not_11_out,
       not_12_out, not_13_out, not_14_out, not_15_out, not_16_out, not_17_out, not_18_out, not_19_out,
       not_20_out, not_21_out, Step2, Step3, Step4, Step5, STOREA0, SUB0, SUB1;
  wire [7:0] sc_1_data_out;

  not not_1 (not_1_out, Instruction[5]);
  not not_2 (not_2_out, Instruction[6]);
  not not_3 (not_3_out, Instruction[7]);
  not not_4 (not_4_out, Instruction[4]);
  not not_5 (not_5_out, Instruction[6]);
  not not_6 (not_6_out, Instruction[7]);
  not not_7 (not_7_out, Instruction[6]);
  not not_8 (not_8_out, Instruction[7]);
  not not_9 (not_9_out, Instruction[4]);
  not not_10 (not_10_out, Instruction[5]);
  not not_11 (not_11_out, Instruction[7]);
  not not_12 (not_12_out, Instruction[5]);
  not not_13 (not_13_out, Instruction[7]);
  not not_14 (not_14_out, Instruction[4]);
  not not_15 (not_15_out, Instruction[7]);
  not not_16 (not_16_out, Instruction[7]);
  not not_17 (not_17_out, Instruction[4]);
  not not_18 (not_18_out, Instruction[5]);
  not not_19 (not_19_out, Instruction[6]);
  not not_20 (not_20_out, Instruction[4]);
  and and_1 (and_1_out, Instruction[4], not_1_out, not_2_out, not_3_out);
  and and_2 (and_2_out, not_4_out, Instruction[5], not_5_out, not_6_out);
  and and_3 (and_3_out, Instruction[4], Instruction[5], not_7_out, not_8_out);
  and and_4 (and_4_out, not_9_out, not_10_out, Instruction[6], not_11_out);
  and and_5 (and_5_out, Instruction[4], not_12_out, Instruction[6], not_13_out);
  and and_6 (and_6_out, not_14_out, Instruction[5], Instruction[6], not_15_out);
  and and_7 (and_7_out, Instruction[4], Instruction[5], Instruction[6], not_16_out);
  and and_8 (and_8_out, not_17_out, not_18_out, not_19_out, Instruction[7]);
  and and_9 (and_9_out, not_20_out, Instruction[5], Instruction[6], Instruction[7]);
  and and_10 (and_10_out, Instruction[4], Instruction[5], Instruction[6], Instruction[7]);
  not not_21 (not_21_out, CLK);
  and and_11 (ADD0, and_2_out, Step2);
  and and_12 (ADD1, and_2_out, Step3);
  and and_13 (ADD2, and_2_out, Step4);
  and and_14 (SUB0, and_3_out, Step2);
  and and_15 (SUB1, and_3_out, Step3);
  and and_16 (SUB, and_3_out, Step4);
  and and_17 (STOREA0, and_4_out, Step2);
  and and_18 (RI, and_4_out, Step3);
  and and_19 (LOADI0, and_5_out, Step2);
  and and_20 (JMP0, and_6_out, Step2);
  and and_21 (JMPC0, and_7_out, Instruction[1], Step2);
  and and_22 (JMPZ0, and_8_out, Instruction[0], Step2);
  and and_23 (OI, and_9_out, Step2);
  and and_24 (HLT, and_10_out, Step2);
  and and_25 (LOADA0, and_1_out, Step2);
  and and_26 (LOADA1, and_1_out, Step3);
  SC sc_1 (.CLK(not_21_out), .Reset(Step5), .CE(1'b1), .Data_Out(sc_1_data_out));
  Hex_Digit_Display hex_digit_display_1 (.value(sc_1_data_out[3:0]));  // open: dp
  Decoder #(.select(3)) decoder_1 (
    .out0(CO), .out1(CE), .out2(Step2), .out3(Step3), .out4(Step4), .out5(Step5), .sel(sc_1_data_out[2:0]),
    .en(1'b1));  // open: out6, out7
  or or_1 (MI, CO, LOADA0, ADD0, SUB0, STOREA0);
  or or_2 (RO, CE, LOADA1, ADD1, SUB1);
  or or_3 (IO, LOADA0, ADD0, SUB0, STOREA0, LOADI0, JMP0, JMPC0, JMPZ0);
  or or_4 (AI, LOADA1, ADD2, SUB, LOADI0);
  or or_5 (AO, RI, OI);
  or or_6 (BI, ADD1, SUB1);
  or or_7 (EO, ADD2, SUB);
  or or_8 (Jump, JMP0, JMPC0, JMPZ0);
  or or_9 (FI, ADD2, SUB);

  assign II = CE;
  assign Instruction[2] = Instruction[3];
  // also tied to GND on the sheet: Instruction[3]

  // Other names for the same wires on the sheet: HLT0 = HLT; ZF = Instruction[0]; CF = Instruction[1];
  //   OPcode0 = Instruction[4]; OPcode1 = Instruction[5]; OPcode2 = Instruction[6]; OPcode3 = Instruction[7];
  //   OUT0 = OI; Fetch0 = CO; Step0 = CO; Fetch1 = CE; Step1 = CE; STOREA1 = RI; SUB2 = SUB

  // Notes on the sheet:
  //   Fetch
  //   LOADA(0001)
  //   ADD(0010)
  //   SUB(0011)
  //   STOREA(0100)
  //   LOADI(0101)
  //   JMP(0110)
  //   JMPC(0111)
  //   JMPZ(1000)
  //   OUT(1110)
  //   HLT(1111)
endmodule
