// Logisim project SR-Latch.circ as structural Verilog
module NAND_Gate (
  input  A,
  input  B
);

  wire transistor_1_out;

  Transistor transistor_1 (.in(1'b1), .out(transistor_1_out), .gate(A));
  LED led_1 (.in(transistor_1_out));
  Transistor transistor_2 (.in(1'b1), .out(transistor_1_out), .gate(B));
endmodule

module NOT_Gate (
  input  A,
  output Q
);

  nand nand_1 (Q, A, A);
endmodule

module AND_Gate (
  input  A,
  input  B,
  output Q
);

  wire nand_1_out;

  nand nand_1 (nand_1_out, A, B);
  not not_1 (Q, nand_1_out);
endmodule

module OR_Gate (
  input  A,
  input  B,
  output Q
);

  wire not_1_out, not_2_out;

  not not_1 (not_1_out, A);
  not not_2 (not_2_out, B);
  nand nand_1 (Q, not_1_out, not_2_out);
endmodule

module XOR_Gate (
  input  A,
  input  B,
  output Q
);

  wire n1_out, n2_out, n3_out;

  nand n1 (n1_out, A, B);
  nand n2 (n2_out, A, n1_out);
  nand n3 (n3_out, n1_out, B);
  nand n4 (Q, n2_out, n3_out);
endmodule

module MUX (
  input  A,
  input  Selection,
  input  B,
  output Q
);

  wire n1_out, n2_out, not_1_out;

  not not_1 (not_1_out, Selection);
  nand n1 (n1_out, A, not_1_out);
  nand n2 (n2_out, Selection, B);
  nand n3 (Q, n1_out, n2_out);
endmodule

module MUX8 (
  input  Selection,
  input  [7:0] IN_A,
  input  [7:0] IN_B,
  output [7:0] out_4
);

  Multiplexer multiplexer_1 (.in0(IN_A[0]), .in1(IN_B[0]), .out(out_4[0]), .sel(Selection));
  Multiplexer multiplexer_2 (.in0(IN_A[1]), .in1(IN_B[1]), .out(out_4[1]), .sel(Selection));
  Multiplexer multiplexer_3 (.in0(IN_A[2]), .in1(IN_B[2]), .out(out_4[2]), .sel(Selection));
  Multiplexer multiplexer_4 (.in0(IN_A[3]), .in1(IN_B[3]), .out(out_4[3]), .sel(Selection));
  Multiplexer multiplexer_5 (.in0(IN_A[4]), .in1(IN_B[4]), .out(out_4[4]), .sel(Selection));
  Multiplexer multiplexer_6 (.in0(IN_A[5]), .in1(IN_B[5]), .out(out_4[5]), .sel(Selection));
  Multiplexer multiplexer_7 (.in0(IN_A[6]), .in1(IN_B[6]), .out(out_4[6]), .sel(Selection));
  Multiplexer multiplexer_8 (.in0(IN_A[7]), .in1(IN_B[7]), .out(out_4[7]), .sel(Selection));

  // Other names for the same wires on the sheet: A0 = IN_A[0]; A1 = IN_A[1]; A2 = IN_A[2]; A3 = IN_A[3]; A4 = IN_A[4];
  //   A5 = IN_A[5]; A6 = IN_A[6]; A7 = IN_A[7]; B0 = IN_B[0]; B1 = IN_B[1]; B2 = IN_B[2]; B3 = IN_B[3]; B4 = IN_B[4];
  //   B5 = IN_B[5]; B6 = IN_B[6]; B7 = IN_B[7]; OUT0 = out_4[0]; OUT1 = out_4[1]; OUT2 = out_4[2]; OUT3 = out_4[3];
  //   OUT4 = out_4[4]; OUT5 = out_4[5]; OUT6 = out_4[6]; OUT7 = out_4[7]
endmodule

module MUX8x4 (
  input  [7:0] IN_0,
  input  [7:0] IN_1,
  input  [7:0] IN_2,
  input  [7:0] IN_3,
  input  [1:0] SELECTION,
  output [7:0] Q
);

  wire [7:0] multiplexer_1_out, multiplexer_2_out;

  Multiplexer #(.width(8)) multiplexer_1 (.in0(IN_0), .in1(IN_1), .out(multiplexer_1_out), .sel(SELECTION[0]));
  Multiplexer #(.width(8)) multiplexer_2 (.in0(IN_2), .in1(IN_3), .out(multiplexer_2_out), .sel(SELECTION[0]));
  Multiplexer #(.width(8)) multiplexer_3 (
    .in0(multiplexer_1_out), .in1(multiplexer_2_out), .out(Q), .sel(SELECTION[1]));
endmodule

module MUX8x8 (
  input  [7:0] IN_0,
  input  [7:0] IN_1,
  input  [7:0] IN_2,
  input  [7:0] IN_3,
  input  [2:0] SELECTION,
  input  [7:0] IN_4,
  input  [7:0] IN_5,
  input  [7:0] IN_6,
  input  [7:0] IN_7,
  output [7:0] Q
);

  wire [7:0] multiplexer_1_out, multiplexer_2_out;

  Multiplexer #(.select(2), .width(8)) multiplexer_1 (
    .in0(IN_0), .in1(IN_1), .in2(IN_2), .in3(IN_3), .out(multiplexer_1_out), .sel(SELECTION[1:0]));
  Multiplexer #(.select(2), .width(8)) multiplexer_2 (
    .in0(IN_4), .in1(IN_5), .in2(IN_6), .in3(IN_7), .out(multiplexer_2_out), .sel(SELECTION[1:0]));
  Multiplexer #(.width(8)) multiplexer_3 (
    .in0(multiplexer_1_out), .in1(multiplexer_2_out), .out(Q), .sel(SELECTION[2]));
endmodule

module MUX8x16 (
  input  [7:0] IN_0,
  input  [7:0] IN_1,
  input  [7:0] IN_2,
  input  [7:0] IN_3,
  input  [7:0] IN_4,
  input  [7:0] IN_5,
  input  [7:0] IN_6,
  input  [7:0] IN_7,
  input  [3:0] SELECTION,
  input  [7:0] IN_8,
  input  [7:0] IN_9,
  input  [7:0] IN_10,
  input  [7:0] IN_11,
  input  [7:0] IN_12,
  input  [7:0] IN_13,
  input  [7:0] IN_14,
  input  [7:0] IN_15,
  output [7:0] Q
);

  wire [7:0] multiplexer_1_out, multiplexer_2_out;

  Multiplexer #(.select(3), .width(8)) multiplexer_1 (
    .in0(IN_0), .in1(IN_1), .in2(IN_2), .in3(IN_3), .in4(IN_4), .in5(IN_5), .in6(IN_6), .in7(IN_7),
    .out(multiplexer_1_out), .sel(SELECTION[2:0]));
  Multiplexer #(.select(3), .width(8)) multiplexer_2 (
    .in0(IN_8), .in1(IN_9), .in2(IN_10), .in3(IN_11), .in4(IN_12), .in5(IN_13), .in6(IN_14), .in7(IN_15),
    .out(multiplexer_2_out), .sel(SELECTION[2:0]));
  Multiplexer #(.width(8)) multiplexer_3 (
    .in0(multiplexer_1_out), .in1(multiplexer_2_out), .out(Q), .sel(SELECTION[3]));
endmodule

module Decoder3In (
  input  [2:0] SELECTION,
  input  ENABLE,
  output OUT0,
  output OUT1,
  output OUT2,
  output OUT3,
  output OUT4,
  output OUT5,
  output OUT6,
  output OUT7
);

  wire not_1_out, not_2_out, not_3_out;

  not not_1 (not_1_out, SELECTION[0]);
  not not_2 (not_2_out, SELECTION[1]);
  not not_3 (not_3_out, SELECTION[2]);
  and and_1 (OUT0, not_1_out, not_2_out, not_3_out, ENABLE);
  and and_2 (OUT1, SELECTION[0], not_2_out, not_3_out, ENABLE);
  and and_3 (OUT2, not_1_out, SELECTION[1], not_3_out, ENABLE);
  and and_4 (OUT3, SELECTION[0], SELECTION[1], not_3_out, ENABLE);
  and and_5 (OUT4, not_1_out, not_2_out, SELECTION[2], ENABLE);
  and and_6 (OUT5, SELECTION[0], not_2_out, SELECTION[2], ENABLE);
  and and_7 (OUT6, not_1_out, SELECTION[1], SELECTION[2], ENABLE);
  and and_8 (OUT7, SELECTION[0], SELECTION[1], SELECTION[2], ENABLE);
endmodule

module Decoder4In (
  input  [3:0] SELECTION,
  input  ENABLE,
  output OUT0,
  output OUT8,
  output OUT1,
  output OUT9,
  output OUT2,
  output OUT10,
  output OUT3,
  output OUT11,
  output OUT4,
  output OUT12,
  output OUT5,
  output OUT13,
  output OUT6,
  output OUT14,
  output OUT7,
  output OUT15
);

  wire NOT_IN0, NOT_IN1, NOT_IN2, NOT_IN3;

  not not_1 (NOT_IN0, SELECTION[0]);
  not not_2 (NOT_IN1, SELECTION[1]);
  not not_3 (NOT_IN2, SELECTION[2]);
  not not_4 (NOT_IN3, SELECTION[3]);
  and and_1 (OUT0, NOT_IN0, NOT_IN1, NOT_IN2, NOT_IN3, ENABLE);
  and and_2 (OUT1, SELECTION[0], NOT_IN1, NOT_IN2, NOT_IN3, ENABLE);
  and and_3 (OUT2, NOT_IN0, SELECTION[1], NOT_IN2, NOT_IN3, ENABLE);
  and and_4 (OUT3, SELECTION[0], SELECTION[1], NOT_IN2, NOT_IN3, ENABLE);
  and and_5 (OUT4, NOT_IN0, NOT_IN1, SELECTION[2], NOT_IN3, ENABLE);
  and and_6 (OUT5, SELECTION[0], NOT_IN1, SELECTION[2], NOT_IN3, ENABLE);
  and and_7 (OUT6, NOT_IN0, SELECTION[1], SELECTION[2], NOT_IN3, ENABLE);
  and and_8 (OUT7, SELECTION[0], SELECTION[1], SELECTION[2], NOT_IN3, ENABLE);
  and and_9 (OUT8, NOT_IN0, NOT_IN1, NOT_IN2, SELECTION[3], ENABLE);
  and and_10 (OUT9, SELECTION[0], NOT_IN1, NOT_IN2, SELECTION[3], ENABLE);
  and and_11 (OUT10, NOT_IN0, SELECTION[1], NOT_IN2, SELECTION[3], ENABLE);
  and and_12 (OUT11, SELECTION[0], SELECTION[1], NOT_IN2, SELECTION[3], ENABLE);
  and and_13 (OUT12, NOT_IN0, NOT_IN1, SELECTION[2], SELECTION[3], ENABLE);
  and and_14 (OUT13, SELECTION[0], NOT_IN1, SELECTION[2], SELECTION[3], ENABLE);
  and and_15 (OUT14, NOT_IN0, SELECTION[1], SELECTION[2], SELECTION[3], ENABLE);
  and and_16 (OUT15, SELECTION[0], SELECTION[1], SELECTION[2], SELECTION[3], ENABLE);

  // Other names for the same wires on the sheet: IN0 = SELECTION[0]; IN1 = SELECTION[1]; IN2 = SELECTION[2];
  //   IN3 = SELECTION[3]
endmodule

module ControlledBuffer1 (
  input  Data_In,
  input  Enable,
  output Data_Out
);

  wire and_1_out, nand_1_out, not_1_out;

  not not_1 (not_1_out, Data_In);
  nand nand_1 (nand_1_out, Data_In, Enable);
  and and_1 (and_1_out, not_1_out, Enable);
  Transistor transistor_1 (.in(1'b1), .out(Data_Out), .gate(nand_1_out));
  Transistor #(.\type ("n")) transistor_2 (.in(1'b0), .out(Data_Out), .gate(and_1_out));
endmodule

module ControlledBuffer8 (
  input  Enable,
  input  [7:0] Data_In,
  output [7:0] Data_Out
);

  assign Data_Out[0] = Enable ? Data_In[0] : 1'bz;  // Controlled_Buffer controlled_buffer_1
  assign Data_Out[1] = Enable ? Data_In[1] : 1'bz;  // Controlled_Buffer controlled_buffer_2
  assign Data_Out[2] = Enable ? Data_In[2] : 1'bz;  // Controlled_Buffer controlled_buffer_3
  assign Data_Out[3] = Enable ? Data_In[3] : 1'bz;  // Controlled_Buffer controlled_buffer_4
  assign Data_Out[4] = Enable ? Data_In[4] : 1'bz;  // Controlled_Buffer controlled_buffer_5
  assign Data_Out[5] = Enable ? Data_In[5] : 1'bz;  // Controlled_Buffer controlled_buffer_6
  assign Data_Out[6] = Enable ? Data_In[6] : 1'bz;  // Controlled_Buffer controlled_buffer_7
  assign Data_Out[7] = Enable ? Data_In[7] : 1'bz;  // Controlled_Buffer controlled_buffer_8
endmodule

module Half_Adder (
  input  IN_A,
  input  IN_B,
  output Carry,
  output Sum
);

  and and_1 (Carry, IN_A, IN_B);
  xor xor_1 (Sum, IN_A, IN_B);
endmodule

module Full_Adder (
  input  IN_A,
  input  IN_B,
  input  IN_C,
  output Carry,
  output Sum
);

  wire half_adder_1_carry, half_adder_1_sum, half_adder_2_carry;

  Half_Adder half_adder_1 (.IN_A(IN_A), .IN_B(IN_B), .Carry(half_adder_1_carry), .Sum(half_adder_1_sum));
  or or_1 (Carry, half_adder_1_carry, half_adder_2_carry);
  Half_Adder half_adder_2 (.IN_A(half_adder_1_sum), .IN_B(IN_C), .Carry(half_adder_2_carry), .Sum(Sum));
endmodule

module ALU (
  input  [7:0] IN_A,
  input  [7:0] IN_B,
  input  SU,
  input  EO,
  output CF,
  output [7:0] Sum,
  output ZF
);

  wire and_1_out, and_2_out, full_adder_1_carry, full_adder_2_carry, full_adder_3_carry, full_adder_4_carry,
       full_adder_5_carry, full_adder_6_carry, full_adder_7_carry, IN_B0, IN_B1, IN_B2, IN_B3, IN_B4, IN_B5,
       IN_B6, IN_B7, nor_1_out, nor_2_out, nor_3_out, nor_4_out, OUT_0, OUT_1, OUT_2, OUT_3, OUT_4, OUT_5,
       OUT_6, OUT_7;

  xor xor_1 (IN_B7, SU, IN_B[7]);
  xor xor_2 (IN_B6, SU, IN_B[6]);
  xor xor_3 (IN_B5, SU, IN_B[5]);
  Full_Adder full_adder_1 (.IN_A(IN_A[0]), .IN_B(SU), .IN_C(IN_B0), .Carry(full_adder_1_carry), .Sum(OUT_0));
  xor xor_4 (IN_B4, SU, IN_B[4]);
  xor xor_5 (IN_B3, SU, IN_B[3]);
  xor xor_6 (IN_B2, SU, IN_B[2]);
  Full_Adder full_adder_2 (
    .IN_A(IN_A[1]), .IN_B(full_adder_1_carry), .IN_C(IN_B1), .Carry(full_adder_2_carry), .Sum(OUT_1));
  assign Sum = EO ? {OUT_7, OUT_6, OUT_5, OUT_4, OUT_3, OUT_2, OUT_1, OUT_0} : 8'bz;  // Controlled_Buffer controlled_buffer_1
  xor xor_7 (IN_B1, SU, IN_B[1]);
  xor xor_8 (IN_B0, SU, IN_B[0]);
  Full_Adder full_adder_3 (
    .IN_A(IN_A[2]), .IN_B(full_adder_2_carry), .IN_C(IN_B2), .Carry(full_adder_3_carry), .Sum(OUT_2));
  Full_Adder full_adder_4 (
    .IN_A(IN_A[3]), .IN_B(full_adder_3_carry), .IN_C(IN_B3), .Carry(full_adder_4_carry), .Sum(OUT_3));
  Full_Adder full_adder_5 (
    .IN_A(IN_A[4]), .IN_B(full_adder_4_carry), .IN_C(IN_B4), .Carry(full_adder_5_carry), .Sum(OUT_4));
  nor nor_1 (nor_1_out, OUT_0, OUT_1);
  nor nor_2 (nor_2_out, OUT_2, OUT_3);
  nor nor_3 (nor_3_out, OUT_4, OUT_5);
  nor nor_4 (nor_4_out, OUT_6, OUT_7);
  Full_Adder full_adder_6 (
    .IN_A(IN_A[5]), .IN_B(full_adder_5_carry), .IN_C(IN_B5), .Carry(full_adder_6_carry), .Sum(OUT_5));
  and and_1 (and_1_out, nor_1_out, nor_2_out);
  and and_2 (and_2_out, nor_3_out, nor_4_out);
  and and_3 (ZF, and_1_out, and_2_out);
  Full_Adder full_adder_7 (
    .IN_A(IN_A[6]), .IN_B(full_adder_6_carry), .IN_C(IN_B6), .Carry(full_adder_7_carry), .Sum(OUT_6));
  Full_Adder full_adder_8 (.IN_A(IN_A[7]), .IN_B(full_adder_7_carry), .IN_C(IN_B7), .Carry(CF), .Sum(OUT_7));

  // Notes on the sheet:
  //   Zero Checker
endmodule

module SRLatch (
  input  S,
  input  R,
  output Q
);

  wire nor_1_out;

  nor nor_1 (nor_1_out, S, Q);
  nor nor_2 (Q, nor_1_out, R);
endmodule

module GatedSRLatch (
  input  S,
  input  E,
  input  R,
  output Q
);

  wire and_1_out, and_2_out, nor_1_out;

  and and_1 (and_1_out, S, E);
  and and_2 (and_2_out, E, R);
  nor nor_1 (nor_1_out, and_1_out, Q);
  nor nor_2 (Q, nor_1_out, and_2_out);
endmodule
